# Fritzing sketch diagrams (saved by Fritzing 0.9.4)
breadboards: 1

parts:
  Arduino = Arduino Uno (Rev3)
  1K = PHOTOCELL [package=photocell]
  R1 = Resistor [tolerance=±5% resistance=1k package="2512 [SMD]"]
  R2 = Resistor [tolerance=±5% resistance=220 package="2512 [SMD]"]
  LED1_IR = LEDs [package=led10mm]

nets:
  N1: Arduino.A0, 1K.P$2, R1.Pin_0
  N2: Arduino.D13/SCK, LED1_IR.A
  N3: Arduino.5V, R1.Pin_1
  N4: Arduino.GND, 1K.P$1, R2.Pin_1
  N5: R2.Pin_0, LED1_IR.C
